# Fritzing sketch DS18B20_Huzzah schema (saved by Fritzing 0.9.3b)
breadboards: 1

parts:
  DS1 = DS18B20 1-Wire Temperature Sensor [part_number=DS18B20]
  R1 = Resistor [tolerance=±5% resistance=10k package="0603 [SMD]"]
  Part1 = Adafruit Feather HUZZAH ESP8266 [part_number="Adafruit #2821"]

nets (from the breadboard view):
  VDD: DS1.VDD, R1.Pin_1, Part1.3.3V
  N1: DS1.DQ, R1.Pin_0, Part1.GPIO0
  GND: DS1.GND, Part1.GND

custom parts:
  Adafruit Feather HUZZAH ESP8266: his is the Adafruit Feather HUZZAH ESP8266 - our take on an 'all-in-one' ESP8266 WiFi development board with built in USB and battery charging. Its an ESP8266 WiFi module with all the extras you need, ready to rock! We have other boards in the Feather family, check'em out here. At the Feather HUZZAH's heart is an ESP8266 WiFi microcontroller clocked at 80 MHz and at 3.3V logic. This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

// code stored in the sketch: dummy.ino

